# Fritzing sketch Wrist Transmitter - Simple (saved by Fritzing 0.9.3b)
circuit board: 8.01655cm x 5.08cm
breadboards: 1

parts:
  J1 = female pin header, 15 pins [form="♀ (female)"]
  J2 = female pin header, 15 pins [form="♀ (female)"]
  R1 = Resistor [tolerance=±5% resistance=220 package=THT]
  IC1 = IC, DIP package, 16 pins [chip_label=IC]
  R2 = Resistor [tolerance=±5% resistance=220 package=THT]
  R3 = Resistor [tolerance=±5% resistance=220 package=THT]
  R4 = Resistor [tolerance=±5% resistance=220 package=THT]
  R5 = Resistor [tolerance=±5% resistance=220 package=THT]
  R6 = Resistor [tolerance=±5% resistance=220 package=THT]
  R7 = Resistor [tolerance=±5% resistance=220 package=THT]
  R8 = Resistor [tolerance=±5% resistance=220 package=THT]
  J3 = female pin header, 4 pins [form="♀ (female)"]
  J4 = female pin header, 1 pin [form="♀ (female)"]
  J5 = female pin header, 1 pin [form="♀ (female)"]
  J6 = female pin header, 1 pin [form="♀ (female)"]
  J7 = female pin header, 1 pin [form="♀ (female)"]
  J8 = female pin header, 1 pin [form="♀ (female)"]
  J9 = female pin header, 1 pin [form="♀ (female)"]
  J10 = female pin header, 1 pin [form="♀ (female)"]
  J11 = female pin header, 1 pin [form="♀ (female)"]
  J12 = female pin header, 2 pins [form="♀ (female)"]
  J13 = female pin header, 2 pins [form="♀ (female)"]
  J14 = female pin header, 2 pins [form="♀ (female)"]
  R9 = Resistor [tolerance=±5% resistance=220 package=THT]
  R10 = Resistor [tolerance=±5% resistance=220 package=THT]
  R11 = Resistor [tolerance=±5% resistance=220 package=THT]
  J15 = female pin header, 2 pins [form="♀ (female)"]  # not connected
  J16 = female pin header, 2 pins [form="♀ (female)"]
  R12 = Resistor [tolerance=±5% resistance=220 package=THT]
  J17 = female pin header, 1 pin [form="♀ (female)"]
  J18 = female pin header, 1 pin [form="♀ (female)"]

nets:
  N1: J1.pin4, IC1.pin9, IC1.pin10, IC1.pin11, IC1.pin12, IC1.pin13, IC1.pin14, IC1.pin15, IC1.pin16, J3.pin2, J5.pin1, J9.pin1
  N2: J1.pin5, J16.pin1, J16.pin2, R12.Pin_1
  N3: J1.pin11, J11.pin1
  N4: J1.pin12, J4.pin1
  N5: J2.pin1, J3.pin4
  N6: J2.pin2, J3.pin3
  N7: J2.pin4, R1.Pin_1, R2.Pin_1, R3.Pin_1, R4.Pin_1, R5.Pin_0, R6.Pin_0, R7.Pin_0, R8.Pin_0, J3.pin1, J6.pin1, J7.pin1, R12.Pin_0, J18.pin1
  N8: J2.pin5, R1.Pin_0, IC1.pin1
  N9: J2.pin6, IC1.pin2, R2.Pin_0
  N10: J2.pin7, IC1.pin3, R3.Pin_0
  N11: J2.pin8, IC1.pin4, R4.Pin_0
  N12: J2.pin9, IC1.pin5, R5.Pin_1
  N13: J2.pin10, IC1.pin6, R6.Pin_1
  N14: J2.pin11, IC1.pin7, R7.Pin_1
  N15: J2.pin12, IC1.pin8, R8.Pin_1
  N16: J2.pin13, R10.Pin_1
  N17: J2.pin14, R9.Pin_1
  N18: J2.pin15, R11.Pin_1
  N19: J8.pin1, J10.pin1
  N20: J12.pin1, J13.pin1, J14.pin1, J17.pin1
  N21: J12.pin2, R10.Pin_0
  N22: J13.pin2, R11.Pin_0
  N23: J14.pin2, R9.Pin_0
